# Fritzing sketch shield_circuit_diagram (saved by Fritzing 1.0.1rc)

parts:
  Part1 = Arduino Nano 33 BLE Sense
  Part2 = NeoPixel Stick [part_number=1426]

nets:
  N1: Part1.D5~, Part2.DATAIN
  GND: Part1.GND, Part1.A7, Part2.GND
  3V3: Part1.3V3, Part2.+5V

custom parts:
  Arduino Nano 33 BLE Sense: The Nano 33 BLE Sense (without headers) is Arduino’s 3.3V AI enabled board in the smallest available form factor: 45x18mm! The Arduino Nano 33 BLE Sense is a completely new board on a well-known form factor. It comes with a series of embedded sensors: 9 axis inertial sensor: what makes this board ideal for wearable devices humidity, and temperature sensor: to get highly accurate measurements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
  NeoPixel Stick: Make your own little LED strip arrangement with this stick of NeoPixel LEDs. We crammed 8 of the tiny 5050 (5mm x 5mm) smart RGB LEDs onto a PCB with mounting holes and a chainable design. Use only one microcontroller pin to control as many as you can chain together! Each LED is addressable as the driver chip is inside the LED. Each one has ~18mA constant current drive so the color will be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
